# Fritzing sketch circuit diagram project student ump (saved by Fritzing 0.9.3b)
stripboards: 2

parts:
  IC1 = L293D [package=THT]
  IC2 = L293D [package=THT]
  Part1 = Arduino Mega 2560 (Rev3)
  S1 = H-Bridge with L298N
  S2 = H-Bridge with L298N
  ESP32_-_Back1 = ESP32 - CAM
  M1 = DC Motor
  M2 = DC Motor
  M3 = DC Motor
  M4 = DC Motor
  M5 = DC Motor
  M6 = DC Motor
  M7 = DC Motor
  J1 = Basic Servo
  U1 = Voltage Regulator - 5V [package="TO220 [THT]"]
  HC-SR04_Sensor_1 = HC-SR04 Ultrasonic Distance Sensor
  J2 = female pin header, 8 pins [form="♀ (female)"]
  J3 = female pin header, 8 pins [form="♀ (female)"]
  J2_2 = female alternating pin header, 8 pins [form="♀ (female)"]
  U2 = Voltage Regulator - 5V [package="TO220 [THT]"]
  Power_plug1 = Power plug
  C2 = Ceramic Capacitor [capacitance=100nF package="100 mil [THT, multilayer]"]
  C3 = Ceramic Capacitor [capacitance=100nF package="100 mil [THT, multilayer]"]

nets:
  5V: IC1.Enable_1, IC1.+Vmotor, IC1.Enable_2, IC1.+V, IC2.Enable_1, IC2.+Vmotor, IC2.Enable_2, IC2.+V, Part1.5V, ESP32_-_Back1.5V, HC-SR04_Sensor_1.VCC, J2.pin1, J2.pin8, J3.pin1, J3.pin8, J2_2.pin1, J2_2.pin8, U2.output_voltage
  N1: IC1.In_1, IC1.In_4, J2.pin2
  N2: IC1.Out_1_(_Controlled_by_Enable_1_), IC1.Out_4_(_Controlled_by_Enable_2_), M7.pin_1, J2.pin3
  GND: IC1.0V, IC2.0V, Part1.GND, S1.GND, S2.GND, ESP32_-_Back1.GND, J1.gnd, U1.GND, HC-SR04_Sensor_1.GND, J2.pin4, J2.pin5, J3.pin4, J3.pin5, J2_2.pin4, J2_2.pin5, U2.GND, Power_plug1.GND, C2.1, C3.1
  N3: IC1.Out_2_(_Controlled_by_Enable_1_), IC1.Out_3_(_Controlled_by_Enable_2_), M7.pin_2, J2.pin6
  N4: IC1.In_2, IC1.In_3, Part1.D13_PWM, J2.pin7
  N5: IC2.In_1, IC2.In_4, Part1.D11_PWM, J3.pin2, J2_2.pin2
  N6: IC2.Out_1_(_Controlled_by_Enable_1_), IC2.Out_4_(_Controlled_by_Enable_2_), M1.pin_2, M6.pin_1, J3.pin3, J2_2.pin3
  N7: IC2.Out_2_(_Controlled_by_Enable_1_), IC2.Out_3_(_Controlled_by_Enable_2_), M1.pin_1, M6.pin_2, J3.pin6, J2_2.pin6
  N8: IC2.In_2, IC2.In_3, Part1.D12_PWM, J3.pin7, J2_2.pin7
  N9: Part1.D21/SCL, S2.IN4
  N10: Part1.D20/SDA, S2.IN3
  N11: Part1.D19/RX1, S2.IN2
  N12: Part1.D18/TX1, S2.IN1
  N13: Part1.D17_PWM/RX2, S1.IN4
  N14: Part1.D16_PWM/TX2, S1.IN3
  N15: Part1.D15/RX3, S1.IN2
  N16: Part1.D14/TX3, S1.IN1
  N17: Part1.D10_PWM, HC-SR04_Sensor_1.TRIG
  N18: Part1.D9_PWM, HC-SR04_Sensor_1.ECHO
  12V: Part1.VIN, S1.12V, S2.12V, U1.input_voltage, U2.input_voltage, Power_plug1.VCC, C2.0, C3.0
  N19: Part1.D22, ESP32_-_Back1.GPIO13
  N20: Part1.D24, ESP32_-_Back1.GPIO15
  N21: Part1.D26, ESP32_-_Back1.GPIO14
  N22: Part1.D28, ESP32_-_Back1.GPIO2
  N23: S1.ENA, S1.ENA-5V
  N24: S1.ENB, S1.ENB-5V
  N25: S1.M1-01, M4.pin_2
  N26: S1.M1-02, M4.pin_1
  N27: S1.M2-01, M5.pin_2
  N28: S1.M2-02, M5.pin_1
  N29: S2.ENA, S2.ENA-5V
  N30: S2.ENB, S2.ENB-5V
  N31: S2.M1-01, M3.pin_2
  N32: S2.M1-02, M3.pin_1
  N33: S2.M2-01, M2.pin_2
  N34: S2.M2-02, M2.pin_1
  N35: ESP32_-_Back1.GPIO12, J1.pulse
  N36: J1.vcc, U1.output_voltage

notes:
  9V
  12v bateri
  6V

custom parts:
  H-Bridge with L298N: h-bridge
  ESP32 - CAM: The ESP32-CAM has a very competitive small-size camera module that can operate independently as a minimum system with a footprint of only 27*40.5*4.5mm and a deep sleep current of up to 6mA.
